# Fritzing sketch ambilight (saved by Fritzing 0.9.2b)
circuit board: 10.1776cm x 5.36194cm
breadboards: 1

parts:
  Q1 = npn-Powertransistor [package="TO220 [THT]"]
  Q2 = npn-Powertransistor [package="TO220 [THT]"]
  Q3 = npn-Powertransistor [package="TO220 [THT]"]
  Q4 = npn-Powertransistor [package="TO220 [THT]"]
  Q5 = npn-Powertransistor [package="TO220 [THT]"]
  Q6 = npn-Powertransistor [package="TO220 [THT]"]
  Q7 = npn-Powertransistor [package="TO220 [THT]"]
  Q8 = npn-Powertransistor [package="TO220 [THT]"]
  Q9 = npn-Powertransistor [package="TO220 [THT]"]
  Q10 = npn-Powertransistor [package="TO220 [THT]"]
  Q11 = npn-Powertransistor [package="TO220 [THT]"]
  Q12 = npn-Powertransistor [package="TO220 [THT]"]
  J1 = COMPUTER-PERIPHERAL-POWER [package=computer-peripheral-power]
  J2 = COMPUTER-PERIPHERAL-POWER [package=computer-peripheral-power]
  J3 = COMPUTER-PERIPHERAL-POWER [package=computer-peripheral-power]
  J4 = COMPUTER-PERIPHERAL-POWER [package=computer-peripheral-power]
  J5 = Power Jack [package=power_jack_pth_lock]
  R1 = Resistor [tolerance=±5% resistance=2.2k package="2010 [SMD]"]
  R2 = Resistor [tolerance=±5% resistance=2.2k package="2010 [SMD]"]
  R3 = Resistor [tolerance=±5% resistance=2.2k package="2010 [SMD]"]
  R4 = Resistor [tolerance=±5% resistance=2.2k package="2010 [SMD]"]
  R5 = Resistor [tolerance=±5% resistance=2.2k package="2010 [SMD]"]
  R6 = Resistor [tolerance=±5% resistance=2.2k package="2010 [SMD]"]
  R7 = Resistor [tolerance=±5% resistance=2.2k package="2010 [SMD]"]
  R8 = Resistor [tolerance=±5% resistance=2.2k package="2010 [SMD]"]
  R9 = Resistor [tolerance=±5% resistance=2.2k package="2010 [SMD]"]
  R10 = Resistor [tolerance=±5% resistance=2.2k package="2010 [SMD]"]
  R12 = Resistor [tolerance=±5% resistance=2.2k package="2010 [SMD]"]
  R11 = Resistor [tolerance=±5% resistance=2.2k package="2010 [SMD]"]
  Bauteil1 = Arduino Mega 2560 (Rev3)

nets:
  N1: Q1.base, R1.Pin_0
  N2: Q1.collector, J1.NC
  GND: Q1.emitter, Q2.emitter, Q3.emitter, Q4.emitter, Q5.emitter, Q6.emitter, Q7.emitter, Q8.emitter, Q9.emitter, Q10.emitter, Q11.emitter, Q12.emitter, J5.GND, J5.GNDBREAK, Bauteil1.GND
  N3: Q2.base, R2.Pin_0
  N4: Q2.collector, J1.GND
  N5: Q3.base, R3.Pin_0
  N6: Q3.collector, J1.5V
  N7: Q4.base, R4.Pin_0
  N8: Q4.collector, J2.NC
  N9: Q5.base, R5.Pin_0
  N10: Q5.collector, J2.GND
  N11: Q6.base, R6.Pin_0
  N12: Q6.collector, J2.5V
  N13: Q7.base, R7.Pin_0
  N14: Q7.collector, J3.NC
  N15: Q8.base, R8.Pin_0
  N16: Q8.collector, J3.GND
  N17: Q9.base, R9.Pin_0
  N18: Q9.collector, J3.5V
  N19: Q10.base, R10.Pin_0
  N20: Q10.collector, J4.NC
  N21: Q11.base, R11.Pin_0
  N22: Q11.collector, J4.GND
  N23: Q12.base, R12.Pin_0
  N24: Q12.collector, J4.5V
  12V: J1.12V, J2.12V, J3.12V, J4.12V, J5.PWR
  N25: R1.Pin_1, Bauteil1.D2_PWM
  N26: R2.Pin_1, Bauteil1.D3_PWM
  N27: R3.Pin_1, Bauteil1.D4_PWM
  N28: R4.Pin_1, Bauteil1.D5_PWM
  N29: R5.Pin_1, Bauteil1.D6_PWM
  N30: R6.Pin_1, Bauteil1.D7_PWM
  N31: R7.Pin_1, Bauteil1.D8_PWM
  N32: R8.Pin_1, Bauteil1.D9_PWM
  N33: R9.Pin_1, Bauteil1.D10_PWM
  N34: R10.Pin_1, Bauteil1.D11_PWM
  N35: R12.Pin_1, Bauteil1.D13_PWM
  N36: R11.Pin_1, Bauteil1.D12_PWM
