# Fritzing sketch ambilightv2 (saved by Fritzing 0.9.2b)
circuit board: 10.1776cm x 5.36194cm
breadboards: 1

parts:
  Q1 = npn-Powertransistor [package="TO220 [THT]"]
  Q2 = npn-Powertransistor [package="TO220 [THT]"]
  Q3 = npn-Powertransistor [package="TO220 [THT]"]
  Q4 = npn-Powertransistor [package="TO220 [THT]"]
  Q5 = npn-Powertransistor [package="TO220 [THT]"]
  Q6 = npn-Powertransistor [package="TO220 [THT]"]
  Q7 = npn-Powertransistor [package="TO220 [THT]"]
  Q8 = npn-Powertransistor [package="TO220 [THT]"]
  Q9 = npn-Powertransistor [package="TO220 [THT]"]
  Q10 = npn-Powertransistor [package="TO220 [THT]"]
  Q11 = npn-Powertransistor [package="TO220 [THT]"]
  Q12 = npn-Powertransistor [package="TO220 [THT]"]
  J1 = COMPUTER-PERIPHERAL-POWER [package=computer-peripheral-power]
  J2 = COMPUTER-PERIPHERAL-POWER [package=computer-peripheral-power]
  J3 = COMPUTER-PERIPHERAL-POWER [package=computer-peripheral-power]
  J4 = COMPUTER-PERIPHERAL-POWER [package=computer-peripheral-power]
  J5 = Power Jack [package=power_jack_pth_lock]
  Bauteil1 = Arduino Mega 2560 (Rev3)
  T1 = LM35 Temperature Sensor [package="TO92 [THT]"]
  R10 = Resistor [tolerance=±5% resistance=2.2k package=THT]
  R8 = Resistor [tolerance=±5% resistance=2.2k package=THT]
  R9 = Resistor [tolerance=±5% resistance=2.2k package=THT]
  R12 = Resistor [tolerance=±5% resistance=2.2k package=THT]
  R6 = Resistor [tolerance=±5% resistance=2.2k package=THT]
  R5 = Resistor [tolerance=±5% resistance=2.2k package=THT]
  R7 = Resistor [tolerance=±5% resistance=2.2k package=THT]
  R1 = Resistor [tolerance=±5% resistance=2.2k package=THT]
  R2 = Resistor [tolerance=±5% resistance=2.2k package=THT]
  R3 = Resistor [tolerance=±5% resistance=2.2k package=THT]
  R4 = Resistor [tolerance=±5% resistance=2.2k package=THT]
  R11 = Resistor [tolerance=±5% resistance=2.2k package=THT]

nets:
  N1: Q1.base, R1.Pin_0
  N2: Q1.collector, J1.NC
  GND: Q1.emitter, Q2.emitter, Q3.emitter, Q4.emitter, Q5.emitter, Q6.emitter, Q7.emitter, Q8.emitter, Q9.emitter, Q10.emitter, Q11.emitter, Q12.emitter, J5.GND, J5.GNDBREAK, Bauteil1.GND, T1.GND
  N3: Q2.base, R2.Pin_0
  N4: Q2.collector, J1.GND
  N5: Q3.base, R3.Pin_0
  N6: Q3.collector, J1.5V
  N7: Q4.base, R4.Pin_0
  N8: Q4.collector, J2.NC
  N9: Q5.base, R5.Pin_0
  N10: Q5.collector, J2.GND
  N11: Q6.base, R6.Pin_0
  N12: Q6.collector, J2.5V
  N13: Q7.base, R7.Pin_0
  N14: Q7.collector, J3.NC
  N15: Q8.base, R8.Pin_0
  N16: Q8.collector, J3.GND
  N17: Q9.base, R9.Pin_0
  N18: Q9.collector, J3.5V
  N19: Q10.base, R10.Pin_0
  N20: Q10.collector, J4.NC
  N21: Q11.base, R11.Pin_0
  N22: Q11.collector, J4.GND
  N23: Q12.base, R12.Pin_0
  N24: Q12.collector, J4.5V
  12V: J1.12V, J2.12V, J3.12V, J4.12V, J5.PWR, Bauteil1.VIN
  N25: Bauteil1.A7, T1.Vout
  N26: Bauteil1.D13_PWM, R12.Pin_1
  N27: Bauteil1.D12_PWM, R11.Pin_1
  N28: Bauteil1.D11_PWM, R10.Pin_1
  N29: Bauteil1.D10_PWM, R9.Pin_1
  N30: Bauteil1.D9_PWM, R8.Pin_1
  N31: Bauteil1.D8_PWM, R7.Pin_1
  N32: Bauteil1.5V, T1.+Vs
  N33: Bauteil1.D2_PWM, R3.Pin_1
  N34: Bauteil1.D3_PWM, R2.Pin_1
  N35: Bauteil1.D4_PWM, R1.Pin_1
  N36: Bauteil1.D5_PWM, R6.Pin_1
  N37: Bauteil1.D6_PWM, R5.Pin_1
  N38: Bauteil1.D7_PWM, R4.Pin_1
